// Logisim project BOUDRAA_Imad_Eddine_G06.circ as structural Verilog: 1 circuit, main circuit main
module main (
  input  cause0,
  input  Start_System,
  input  Disk0,
  input  Disk1,
  input  Disk2,
  input  Disk3,
  input  Mask_Level_3,
  input  Room1,
  input  room2,
  input  in_10,
  input  room3,
  input  room4,
  input  room5,
  input  room6,
  input  in_15,
  input  in_16,
  input  cause0_2,
  input  cause1,
  input  cause2,
  input  cause3,
  input  in_21,
  input  in_22,
  input  in_23,
  input  in_24,
  output [1:0] IT_Level,
  output VF,
  output Mask_Level_0,
  output Mask_Level_1,
  output Mask_Level_2,
  output [1:0] Device_Number,
  output [7:0] ADR,
  output Level_1_IT_detected
);

  wire and_1_out, and_2_out, and_3_out, and_4_out, and_5_out, and_6_out, and_7_out, and_8_out, and_9_out,
       and_10_out, and_11_out, and_12_out, and_13_out, and_14_out, and_15_out, and_16_out, and_17_out,
       and_18_out, and_19_out, and_20_out, and_21_out, CLOCK, CTRL_0, CTRL_1, CTRL_2, CTRL_3, d_ff_1_q,
       d_ff_2_q, d_ff_3_q, d_ff_4_q, d_ff_5_q, d_ff_6_q, d_ff_7_q, d_ff_8_q, d_ff_9_q, d_ff_10_q, d_ff_11_q,
       d_ff_12_q, d_ff_13_q, d_ff_14_q, d_ff_15_q, d_ff_16_q, d_ff_21_q, d_ff_22_q, d_ff_23_q, d_ff_24_q,
       d_ff_25_q, d_ff_26_q, d_ff_27_q, d_ff_28_q, d_ff_29_q, d_ff_30_q, d_ff_31_q, d_ff_35_q, d_ff_37_q,
       d_ff_39_q, d_ff_42_q, d_ff_43_q, d_ff_44_q, d_ff_45_q, d_ff_49_q, IT_Flip_Flop_q,
       main_1_it_requet_output, main_2_phase_1, main_2_phase_2, main_2_phase_3, main_2_pulse_2,
       main_2_pulse_3, or_1_out, or_2_out, or_3_out, or_4_out, or_5_out, or_6_out, undriven;
  wire [1:0] controlled_buffer_1_out, d_ff_47_q, main_3_it_level;
  wire [7:0] controlled_buffer_2_out, controlled_buffer_4_out, rom_1_routine_adress;

  D_Flip_Flop d_ff_1 (.clk(CLOCK), .D(Start_System), .Q(d_ff_1_q));  // open: Qn, preset, en, reset
  D_Flip_Flop d_ff_2 (.Q(d_ff_2_q), .preset(1'b1));  // open: clk, D, Qn, en, reset
  D_Flip_Flop d_ff_3 (.clk(CLOCK), .D(Start_System), .Q(d_ff_3_q));  // open: Qn, preset, en, reset
  D_Flip_Flop d_ff_4 (.clk(CLOCK), .D(Start_System), .Q(d_ff_4_q));  // open: Qn, preset, en, reset
  D_Flip_Flop d_ff_5 (.clk(CLOCK), .D(Start_System), .Q(d_ff_5_q));  // open: Qn, preset, en, reset
  D_Flip_Flop d_ff_6 (.clk(undriven), .D(in_21), .Q(d_ff_6_q));  // open: Qn, preset, en, reset
  and and_1 (and_1_out, cause0, d_ff_2_q);
  D_Flip_Flop d_ff_7 (.clk(CLOCK), .D(Start_System), .Q(d_ff_7_q));  // open: Qn, preset, en, reset
  D_Flip_Flop d_ff_8 (.clk(CLOCK), .D(Start_System), .Q(d_ff_8_q));  // open: Qn, preset, en, reset
  D_Flip_Flop d_ff_9 (.clk(undriven), .D(in_22), .Q(d_ff_9_q));  // open: Qn, preset, en, reset
  D_Flip_Flop d_ff_10 (.clk(CLOCK), .D(and_1_out), .Q(d_ff_10_q));  // open: Qn, preset, en, reset
  D_Flip_Flop d_ff_11 (.clk(CLOCK), .D(Start_System), .Q(d_ff_11_q));  // open: Qn, preset, en, reset
  D_Flip_Flop d_ff_12 (.clk(CLOCK), .D(Start_System), .Q(d_ff_12_q));  // open: Qn, preset, en, reset
  and and_2 (and_2_out, Disk0, d_ff_3_q);
  and and_3 (and_3_out, Disk1, d_ff_5_q);
  and and_4 (and_4_out, Disk2, d_ff_7_q);
  and and_5 (and_5_out, Disk3, d_ff_11_q);
  D_Flip_Flop d_ff_13 (.clk(CLOCK), .D(in_15), .Q(d_ff_13_q));  // open: Qn, preset, en, reset
  D_Flip_Flop d_ff_14 (.clk(undriven), .D(in_23), .Q(d_ff_14_q));  // open: Qn, preset, en, reset
  D_Flip_Flop d_ff_15 (.clk(CLOCK), .D(in_16), .Q(d_ff_15_q));  // open: Qn, preset, en, reset
  D_Flip_Flop d_ff_16 (.clk(undriven), .D(in_24), .Q(d_ff_16_q));  // open: Qn, preset, en, reset
  D_Flip_Flop d_ff_17 (.clk(CLOCK), .D(and_2_out), .Q(CTRL_0));  // open: Qn, preset, en, reset
  D_Flip_Flop d_ff_18 (.clk(CLOCK), .D(and_3_out), .Q(CTRL_1));  // open: Qn, preset, en, reset
  D_Flip_Flop d_ff_19 (.clk(CLOCK), .D(and_4_out), .Q(CTRL_2));  // open: Qn, preset, en, reset
  D_Flip_Flop d_ff_20 (.clk(CLOCK), .D(and_5_out), .Q(CTRL_3));  // open: Qn, preset, en, reset
  and and_6 (and_6_out, cause0_2, d_ff_6_q);
  and and_7 (and_7_out, cause1, d_ff_9_q);
  and and_8 (and_8_out, cause2, d_ff_14_q);
  and and_9 (and_9_out, cause3, d_ff_16_q);
  D_Flip_Flop d_ff_21 (.clk(CLOCK), .D(and_10_out), .Q(d_ff_21_q));  // open: Qn, preset, en, reset
  and and_10 (and_10_out, Room1, d_ff_1_q);
  D_Flip_Flop d_ff_22 (.clk(CLOCK), .D(and_11_out), .Q(d_ff_22_q));  // open: Qn, preset, en, reset
  and and_11 (and_11_out, room2, d_ff_4_q);
  D_Flip_Flop d_ff_23 (.clk(CLOCK), .D(and_12_out), .Q(d_ff_23_q));  // open: Qn, preset, en, reset
  and and_12 (and_12_out, room3, d_ff_8_q);
  D_Flip_Flop d_ff_24 (.clk(CLOCK), .D(and_13_out), .Q(d_ff_24_q));  // open: Qn, preset, en, reset
  and and_13 (and_13_out, room4, d_ff_12_q);
  and and_14 (and_14_out, room5, d_ff_13_q);
  and and_15 (and_15_out, room6, d_ff_15_q);
  D_Flip_Flop d_ff_25 (.clk(CLOCK), .D(and_6_out), .Q(d_ff_25_q));  // open: Qn, preset, en, reset
  D_Flip_Flop d_ff_26 (.clk(CLOCK), .D(and_7_out), .Q(d_ff_26_q));  // open: Qn, preset, en, reset
  D_Flip_Flop d_ff_27 (.clk(CLOCK), .D(and_8_out), .Q(d_ff_27_q));  // open: Qn, preset, en, reset
  D_Flip_Flop d_ff_28 (.clk(CLOCK), .D(and_9_out), .Q(d_ff_28_q));  // open: Qn, preset, en, reset
  Clock u_CLOCK (.out(CLOCK));
  or or_1 (or_1_out, CTRL_0, CTRL_1, CTRL_2, CTRL_3);
  D_Flip_Flop d_ff_29 (.clk(CLOCK), .D(and_14_out), .Q(d_ff_29_q));  // open: Qn, preset, en, reset
  D_Flip_Flop d_ff_30 (.clk(CLOCK), .D(and_15_out), .Q(d_ff_30_q));  // open: Qn, preset, en, reset
  or or_2 (or_2_out, d_ff_21_q, d_ff_22_q, d_ff_23_q, d_ff_24_q, d_ff_29_q, d_ff_30_q);
  or or_3 (or_3_out, d_ff_25_q, d_ff_26_q, d_ff_27_q, d_ff_28_q);
  D_Flip_Flop d_ff_31 (.clk(CLOCK), .D(Start_System), .Q(d_ff_31_q));  // open: Qn, preset, en, reset
  D_Flip_Flop #(.trigger("high")) d_ff_32 (
    .clk(CLOCK), .D(controlled_buffer_2_out[7]));  // open: Q, Qn, preset, en, reset
  D_Flip_Flop #(.trigger("high")) d_ff_33 (
    .clk(CLOCK), .D(controlled_buffer_2_out[5]));  // open: Q, Qn, preset, en, reset
  D_Flip_Flop #(.trigger("high")) d_ff_34 (
    .clk(CLOCK), .D(controlled_buffer_2_out[6]));  // open: Q, Qn, preset, en, reset
  D_Flip_Flop d_ff_35 (.clk(CLOCK), .D(Start_System), .Q(d_ff_35_q));  // open: Qn, preset, en, reset
  Daisy_Chain_main main_1 (
    .ACK_IN(or_4_out), .CTL_0(CTRL_0), .CTL_1(CTRL_1), .CTL_2(CTRL_2),
    .IT_Requet_Output(main_1_it_requet_output), .CLOCK(CLOCK), .CTL_3(CTRL_3), .DEVICE_NUMBER(Device_Number),
    .ACK_OUT(in_10));
  Comparator #(.width(2)) comparator_1 (.a(IT_Level), .b(2'b01), .eq(Level_1_IT_detected));  // open: gt, lt
  D_Flip_Flop #(.trigger("high")) d_ff_36 (
    .clk(CLOCK), .D(controlled_buffer_2_out[4]));  // open: Q, Qn, preset, en, reset
  D_Flip_Flop d_ff_37 (.clk(CLOCK), .D(Start_System), .Q(d_ff_37_q));  // open: Qn, preset, en, reset
  assign controlled_buffer_1_out = main_2_pulse_2 ? Device_Number : 2'bz;  // Controlled_Buffer controlled_buffer_1
  Phase_Distributor_main main_2 (
    .CLOCK(CLOCK), .IT_request(and_16_out), .Phase_1(main_2_phase_1), .Pulse_2(main_2_pulse_2),
    .Phase_2(main_2_phase_2), .Pulse_3(main_2_pulse_3), .Phase_3(main_2_phase_3));  // open: Pulse_0, Phase_0, Pulse_1
  and and_16 (and_16_out, main_1_it_requet_output, Level_1_IT_detected);
  D_Flip_Flop #(.trigger("high")) d_ff_38 (
    .clk(CLOCK), .D(controlled_buffer_2_out[3]));  // open: Q, Qn, preset, en, reset
  D_Flip_Flop d_ff_39 (.clk(CLOCK), .D(Mask_Level_3), .Q(d_ff_39_q));  // open: Qn, preset, en, reset
  D_Flip_Flop #(.trigger("high")) d_ff_40 (
    .clk(CLOCK), .D(controlled_buffer_2_out[2]));  // open: Q, Qn, preset, en, reset
  and and_17 (and_17_out, d_ff_10_q, d_ff_31_q);
  and and_18 (and_18_out, or_1_out, d_ff_35_q);
  and and_19 (and_19_out, or_2_out, d_ff_37_q);
  and and_20 (and_20_out, or_3_out, d_ff_39_q);
  D_Flip_Flop #(.trigger("high")) d_ff_41 (
    .clk(CLOCK), .D(controlled_buffer_2_out[1]));  // open: Q, Qn, preset, en, reset
  D_Flip_Flop d_ff_42 (.clk(CLOCK), .D(and_17_out), .Q(d_ff_42_q));  // open: Qn, preset, en, reset
  D_Flip_Flop d_ff_43 (.clk(CLOCK), .D(and_18_out), .Q(d_ff_43_q));  // open: Qn, preset, en, reset
  D_Flip_Flop d_ff_44 (.clk(CLOCK), .D(and_19_out), .Q(d_ff_44_q));  // open: Qn, preset, en, reset
  D_Flip_Flop d_ff_45 (.clk(CLOCK), .D(and_20_out), .Q(d_ff_45_q));  // open: Qn, preset, en, reset
  D_Flip_Flop #(.trigger("high")) d_ff_46 (
    .clk(CLOCK), .D(controlled_buffer_1_out[1]), .Q(d_ff_47_q[1]));  // open: Qn, preset, en, reset
  D_Flip_Flop #(.trigger("high")) d_ff_47 (
    .clk(CLOCK), .D(controlled_buffer_1_out[0]), .Q(d_ff_47_q[0]));  // open: Qn, preset, en, reset
  or or_4 (or_4_out, main_2_phase_1, main_2_phase_2, main_2_phase_3);
  D_Flip_Flop #(.trigger("high")) d_ff_48 (
    .clk(CLOCK), .D(controlled_buffer_2_out[0]));  // open: Q, Qn, preset, en, reset
  or or_5 (or_5_out, d_ff_42_q, d_ff_43_q, d_ff_44_q, d_ff_45_q);
  or or_6 (or_6_out, main_2_phase_2, main_2_phase_3);
  assign controlled_buffer_2_out = main_2_pulse_3 ? controlled_buffer_4_out : 8'bz;  // Controlled_Buffer controlled_buffer_2
  assign IT_Level = and_21_out ? main_3_it_level : 2'bz;  // Controlled_Buffer controlled_buffer_3
  IT_Level_Priority_Encoder_main main_3 (
    .Lvl3(d_ff_45_q), .Lvl2(d_ff_44_q), .Lvl1(d_ff_43_q), .Lvl0(d_ff_42_q), .IT_Level(main_3_it_level));
  D_Flip_Flop d_ff_49 (.clk(CLOCK), .D(Start_System), .Q(d_ff_49_q));  // open: Qn, preset, en, reset
  assign controlled_buffer_4_out = main_2_phase_3 ? ADR : 8'bz;  // Controlled_Buffer controlled_buffer_4
  and and_21 (and_21_out, or_5_out, d_ff_49_q);
  ROM rom_1 (.Cause_Number(d_ff_47_q), .Signal(or_6_out), .routine_adress(rom_1_routine_adress));
  assign ADR = or_6_out ? rom_1_routine_adress : 8'bz;  // Controlled_Buffer controlled_buffer_5
  D_Flip_Flop IT_Flip_Flop (
    .clk(CLOCK), .D(and_21_out), .Q(IT_Flip_Flop_q), .Qn(IT_Flip_Flop_q));  // open: preset, en, reset

  assign Mask_Level_0 = Start_System;
  assign Mask_Level_1 = Start_System;
  assign Mask_Level_2 = Start_System;
  assign VF = Start_System;

  // Other names for the same wires on the sheet: SYSTEM_START = Start_System

  // Notes on the sheet:
  //   Level 0 : Power Failures
  //   Inhibition Register (0 to inhibit and 1 to activate)
  //   Level 1 : Management
  //   Starting the system puts the inhibition and mask to one 
  //   Level 2 : Alarem System
  //   Level 3 :Reserved level
  //   PC
  //   IRAR
  //   RAR
  //   OROM
  //   TDA
  //   ROM
endmodule
