// Logisim project Daisy Chain.circ as structural Verilog: 1 circuit, main circuit main
module main (
  input  ACK_IN,
  input  CLOCK,
  input  CTL_3,
  input  CTL_0,
  input  CTL_1,
  input  CTL_2,
  output [1:0] DEVICE_NUMBER,
  output IT_Requet_Output,
  output ACK_OUT
);

  wire and_1_out, and_2_out, and_3_out, and_4_out, d_ff_1_q, d_ff_2_q, d_ff_3_q, d_ff_4_q, not_1_out,
       not_2_out, not_3_out, not_5_out;
  wire [1:0] controlled_buffer_1_out, priority_encoder_1_out;

  or or_1 (IT_Requet_Output, d_ff_4_q, d_ff_3_q, d_ff_2_q, d_ff_1_q);
  and and_1 (and_1_out, ACK_IN, not_1_out);
  not not_1 (not_1_out, d_ff_1_q);
  D_Flip_Flop d_ff_1 (.clk(CLOCK), .D(CTL_0), .Q(d_ff_1_q));  // open: Qn, preset, en, reset
  D_Flip_Flop d_ff_2 (.clk(CLOCK), .D(CTL_1), .Q(d_ff_2_q));  // open: Qn, preset, en, reset
  not not_2 (not_2_out, d_ff_2_q);
  and and_2 (and_2_out, and_1_out, not_2_out);
  Priority_Encoder #(.select(2), .disabled(0)) priority_encoder_1 (
    .in0(d_ff_4_q), .in1(d_ff_3_q), .in2(d_ff_2_q), .in3(d_ff_1_q), .out(priority_encoder_1_out));  // open: gs, en_out, en_in
  D_Flip_Flop d_ff_3 (.clk(CLOCK), .D(CTL_2), .Q(d_ff_3_q));  // open: Qn, preset, en, reset
  not not_3 (not_3_out, d_ff_3_q);
  and and_3 (and_3_out, and_2_out, not_3_out);
  D_Flip_Flop d_ff_4 (.clk(CLOCK), .D(CTL_3), .Q(d_ff_4_q));  // open: Qn, preset, en, reset
  assign controlled_buffer_1_out = and_4_out ? priority_encoder_1_out : 2'bz;  // Controlled_Buffer controlled_buffer_1
  and and_4 (and_4_out, IT_Requet_Output, ACK_IN);
  assign DEVICE_NUMBER = ~controlled_buffer_1_out;  // NOT_Gate not_4, 2 bits wide
  and and_5 (ACK_OUT, and_3_out, not_5_out);
  not not_5 (not_5_out, d_ff_4_q);

  // Notes on the sheet:
  //   DAISY CHAIN TO IMPLEMENT IN THE TP
endmodule
