// Logisim project IT_Level Priority Encoder.circ as structural Verilog: 1 circuit, main circuit main
module main (
  input  Lvl3,
  input  Lvl2,
  input  Lvl1,
  input  Lvl0,
  output [1:0] IT_Level
);

  wire and_1_out, not_1_out, or_2_out;
  wire [1:0] controlled_buffer_1_out, or_3_out;

  not not_1 (not_1_out, Lvl1);
  or or_1 (or_3_out[1], Lvl1, Lvl0);
  or or_2 (or_2_out, Lvl3, Lvl2, Lvl1, Lvl0);
  and and_1 (and_1_out, Lvl2, not_1_out);
  or or_3 (or_3_out[0], and_1_out, Lvl0);
  assign controlled_buffer_1_out = or_2_out ? or_3_out : 2'bz;  // Controlled_Buffer controlled_buffer_1
  assign IT_Level = ~controlled_buffer_1_out;  // NOT_Gate not_2, 2 bits wide
endmodule
