// Logisim project Phase Distributor.circ as structural Verilog: 1 circuit, main circuit main
module main (
  input  CLOCK,
  input  IT_request,
  output Phase_0,
  output Phase_1,
  output Phase_2,
  output Phase_3,
  output Pulse_0,
  output Pulse_1,
  output Pulse_2,
  output Pulse_3
);

  wire [1:0] counter_1_q;

  and and_1 (Pulse_0, CLOCK, Phase_0);
  Counter #(.width(2), .max('h3)) counter_1 (
    .count(IT_request), .Q(counter_1_q), .clk(CLOCK));  // open: load, D, carry, clr
  and and_2 (Pulse_1, CLOCK, Phase_1);
  Decoder #(.select(2), .enable("false")) decoder_1 (
    .out0(Phase_0), .out1(Phase_1), .out2(Phase_2), .out3(Phase_3), .sel(counter_1_q));
  and and_3 (Pulse_2, CLOCK, Phase_2);
  and and_4 (Pulse_3, CLOCK, Phase_3);
endmodule
