// Logisim project ROM.circ as structural Verilog: 1 circuit, main circuit @ ROM
module ROM (
  input  [1:0] Cause_Number,
  input  Signal,
  output [7:0] routine_adress
);

  wire decoder_1_out0, decoder_1_out1, decoder_1_out2, decoder_1_out3;
  wire [1:0] controlled_buffer_1_out;

  Decoder #(.select(2), .enable("false")) decoder_1 (
    .out0(decoder_1_out0), .out1(decoder_1_out1), .out2(decoder_1_out2), .out3(decoder_1_out3),
    .sel(controlled_buffer_1_out));
  assign controlled_buffer_1_out = Signal ? Cause_Number : 2'bz;  // Controlled_Buffer controlled_buffer_1
  Pull_Resistor pull_resistor_1 (.node(routine_adress[6]));
  Pull_Resistor pull_resistor_2 (.node(routine_adress[7]));
  Transistor #(.\type ("n")) transistor_1 (.in(1'b1), .out(routine_adress[6]), .gate(decoder_1_out3));
  Pull_Resistor pull_resistor_3 (.node(routine_adress[5]));
  Transistor #(.\type ("n")) transistor_2 (.in(1'b1), .out(routine_adress[5]), .gate(decoder_1_out2));
  Pull_Resistor pull_resistor_4 (.node(routine_adress[4]));
  Transistor #(.\type ("n")) transistor_3 (.in(1'b1), .out(routine_adress[3]), .gate(decoder_1_out0));
  Transistor #(.\type ("n")) transistor_4 (.in(1'b1), .out(routine_adress[3]), .gate(decoder_1_out1));
  Transistor #(.\type ("n")) transistor_5 (.in(1'b1), .out(routine_adress[4]), .gate(decoder_1_out1));
  Transistor #(.\type ("n")) transistor_6 (.in(1'b1), .out(routine_adress[4]), .gate(decoder_1_out2));
  Pull_Resistor pull_resistor_5 (.node(routine_adress[2]));
  Pull_Resistor pull_resistor_6 (.node(routine_adress[3]));
  Transistor #(.\type ("n")) transistor_7 (.in(1'b1), .out(routine_adress[2]), .gate(decoder_1_out0));
  Transistor #(.\type ("n")) transistor_8 (.in(1'b1), .out(routine_adress[2]), .gate(decoder_1_out1));
  Transistor #(.\type ("n")) transistor_9 (.in(1'b1), .out(routine_adress[2]), .gate(decoder_1_out3));
  Pull_Resistor pull_resistor_7 (.node(routine_adress[1]));
  Transistor #(.\type ("n")) transistor_10 (.in(1'b1), .out(routine_adress[1]), .gate(decoder_1_out0));
  Transistor #(.\type ("n")) transistor_11 (.in(1'b1), .out(routine_adress[1]), .gate(decoder_1_out3));
  Pull_Resistor pull_resistor_8 (.node(routine_adress[0]));
  Transistor #(.\type ("n")) transistor_12 (.in(1'b1), .out(routine_adress[0]), .gate(decoder_1_out0));
endmodule
